// Logisim project 3. Logisim Circuit.circ as structural Verilog: 4 circuits, main circuit main
module main (
);

  wire _0, _1, _2, _3, _4, and_2_out, Clear_All_out, control_unit_1_fetch_r_en, control_unit_1_mem_write,
       control_unit_1_mem_write_mux, control_unit_1_mux_imm_en, control_unit_1_mux_imm_select_line,
       control_unit_1_mux_r1r2_en, control_unit_1_mux_r1r2_select, control_unit_1_muxrb_en,
       control_unit_1_muxy_en, control_unit_1_muxy_select_line, control_unit_1_pc_register_en,
       control_unit_1_register_reset, control_unit_1_writeback_dmx_en, multiplexer_2_out, not_1_out,
       not_2_out, not_3_out, not_4_out, not_5_out, not_6_out, not_7_out, not_8_out, not_9_out, not_10_out,
       not_11_out, not_12_out, or_1_out, r0_en, r1_en, r2_en, r3_en, r4_en, r5_en, r6_en, r7_en,
       Reset_PC_out, sys_clk_out;
  wire [1:0] control_unit_1_alu_mux;
  wire [2:0] counter_1_q;
  wire [3:0] multiplexer_4_out, multiplexer_5_out;
  wire [7:0] adder_1_out, multiplexer_1_out, PC_temp_q;
  wire [31:0] alu_1_out_3, alu_1_out_4, alu_1_out_5, alu_1_out_6, bit_extender_1_out, IR_q,
       multiplexer_3_out, multiplexer_6_out, multiplexer_7_out, multiplexer_8_out, multiplexer_9_out, r0_in,
       r0_out, r1_in, r1_out, r2_in, r2_out, r3_in, r3_out, r4_in, r4_out, r5_in, r5_out, r6_in, r6_out,
       r7_in, r7_out, RA_q, ram_1_data, RB_q, RY_q, RZ_q;

  Adder adder_1 (.a(8'h1), .b(PC_temp_q), .out(adder_1_out));  // open: cin, cout
  Register PC_temp (
    .D(adder_1_out), .en(control_unit_1_pc_register_en), .Q(PC_temp_q), .clk(multiplexer_2_out),
    .clr(Reset_PC_out));
  Button Reset_PC (.out(Reset_PC_out));
  not not_1 (not_1_out, control_unit_1_mem_write);
  Multiplexer #(.width(8)) multiplexer_1 (
    .in0(PC_temp_q), .in1(RZ_q[7:0]), .out(multiplexer_1_out), .sel(control_unit_1_mem_write_mux), .en(1'b1));
  Counter #(.width(3), .max('h7)) counter_1 (
    .count(1'b1), .Q(counter_1_q), .clk(multiplexer_2_out), .clr(or_1_out));  // open: load, D, carry
  or or_1 (or_1_out, Reset_PC_out, and_2_out);
  RAM #(.dataWidth(32), .bus("separate")) ram_1 (
    .addr(multiplexer_1_out), .din(RB_q), .data(ram_1_data), .str(control_unit_1_mem_write),
    .clk(multiplexer_2_out), .ld(not_1_out), .clr(Clear_All_out));  // open: sel
  Button Clear_All (.out(Clear_All_out));
  and and_1 (_0, not_3_out, not_2_out, not_5_out);
  not not_2 (not_2_out, counter_1_q[1]);
  not not_3 (not_3_out, counter_1_q[0]);
  not not_4 (not_4_out, counter_1_q[1]);
  and and_2 (and_2_out, counter_1_q[2], not_4_out, counter_1_q[0]);
  Register #(.width(32)) IR (
    .D(ram_1_data), .en(control_unit_1_fetch_r_en), .Q(IR_q), .clk(multiplexer_2_out), .clr(Reset_PC_out));
  and and_3 (_1, not_6_out, not_7_out, counter_1_q[0]);
  not not_5 (not_5_out, counter_1_q[2]);
  not not_6 (not_6_out, counter_1_q[2]);
  not not_7 (not_7_out, counter_1_q[1]);
  and and_4 (_2, not_8_out, counter_1_q[1], not_9_out);
  not not_8 (not_8_out, counter_1_q[2]);
  assign bit_extender_1_out = {{16{1'b0}}, IR_q[15:0]};  // Bit_Extender bit_extender_1
  and and_5 (_3, not_10_out, counter_1_q[1], counter_1_q[0]);
  not not_9 (not_9_out, counter_1_q[0]);
  not not_10 (not_10_out, counter_1_q[2]);
  Control_Unit control_unit_1 (
    .in_4(IR_q[31:28]), .fetch_R_en(control_unit_1_fetch_r_en), .mem_write(control_unit_1_mem_write),
    .mem_write_mux(control_unit_1_mem_write_mux), .mux_r1r2_select(control_unit_1_mux_r1r2_select),
    .mux_r1r2_en(control_unit_1_mux_r1r2_en), .muxRB_en(control_unit_1_muxrb_en),
    .mux_imm_select_line(control_unit_1_mux_imm_select_line), .mux_imm_en(control_unit_1_mux_imm_en),
    .writeback_dmx_en(control_unit_1_writeback_dmx_en), .muxY_select_line(control_unit_1_muxy_select_line),
    .muxY_en(control_unit_1_muxy_en), .ALU_mux(control_unit_1_alu_mux),
    .register_reset(control_unit_1_register_reset), .pc_register_en(control_unit_1_pc_register_en),
    .in_2(_0), .in_3(_4), .in_1(_3));  // open: muxRA_en
  and and_6 (_4, not_12_out, not_11_out, counter_1_q[2]);
  not not_11 (not_11_out, counter_1_q[1]);
  not not_12 (not_12_out, counter_1_q[0]);
  register_en register_en_1 (
    .in_1(IR_q[27:24]), .out_4(r0_en), .out_5(r1_en), .out_6(r2_en), .out_7(r3_en), .out_8(r4_en),
    .out_9(r5_en), .out_10(r6_en), .out_11(r7_en), .in_2(control_unit_1_writeback_dmx_en), .in_3(IR_q[31:28]));
  Multiplexer multiplexer_2 (
    .in0(sys_clk_out), .in1(1'b0), .out(multiplexer_2_out), .sel(control_unit_1_muxy_en), .en(1'b1));
  Clock sys_clk (.out(sys_clk_out));
  Multiplexer #(.width(32)) multiplexer_3 (
    .in0(ram_1_data), .in1(RZ_q), .out(multiplexer_3_out), .sel(control_unit_1_muxy_select_line), .en(1'b1));
  Multiplexer #(.width(4)) multiplexer_4 (
    .in0(IR_q[19:16]), .in1(IR_q[23:20]), .out(multiplexer_4_out), .sel(control_unit_1_mux_r1r2_select),
    .en(control_unit_1_mux_r1r2_en));
  Multiplexer #(.width(4)) multiplexer_5 (
    .in0(IR_q[23:20]), .in1(IR_q[19:16]), .out(multiplexer_5_out), .sel(control_unit_1_mux_r1r2_select),
    .en(control_unit_1_mux_r1r2_en));
  Register #(.width(32)) RY (
    .D(multiplexer_3_out), .Q(RY_q), .clk(multiplexer_2_out), .clr(control_unit_1_register_reset));  // open: en
  Demultiplexer #(.select(4), .width(32)) demultiplexer_1 (
    .out0(r0_in), .out1(r1_in), .out2(r2_in), .out3(r3_in), .out4(r4_in), .out5(r5_in), .out6(r6_in),
    .out7(r7_in), .in(RY_q), .sel(IR_q[27:24]), .en(control_unit_1_writeback_dmx_en));  // open: out8, out9, out10, out11, out12, out13, out14, out15
  Multiplexer #(.select(4), .width(32)) multiplexer_6 (
    .in0(r0_out), .in1(r1_out), .in2(r2_out), .in3(r3_out), .in4(r4_out), .in5(r5_out), .in6(r6_out),
    .in7(r7_out), .out(multiplexer_6_out), .sel(multiplexer_4_out), .en(control_unit_1_muxrb_en));  // open: in8, in9, in10, in11, in12, in13, in14, in15
  Register #(.width(32)) RA (
    .D(multiplexer_6_out), .Q(RA_q), .clk(multiplexer_2_out), .clr(control_unit_1_register_reset));  // open: en
  Register #(.width(32)) R0 (.D(r0_in), .en(r0_en), .Q(r0_out), .clk(multiplexer_2_out));  // open: clr
  Register #(.width(32)) R2 (.D(r2_in), .en(r2_en), .Q(r2_out), .clk(multiplexer_2_out));  // open: clr
  Register #(.width(32)) R4 (.D(r4_in), .en(r4_en), .Q(r4_out), .clk(multiplexer_2_out));  // open: clr
  Register #(.width(32)) R6 (.D(r6_in), .en(r6_en), .Q(r6_out), .clk(multiplexer_2_out));  // open: clr
  ALU alu_1 (
    .in_1(RA_q), .in_2(multiplexer_9_out), .out_3(alu_1_out_3), .out_4(alu_1_out_4), .out_5(alu_1_out_5),
    .out_6(alu_1_out_6));
  Multiplexer #(.select(2), .width(32)) multiplexer_7 (
    .in0(alu_1_out_3), .in1(alu_1_out_4), .in2(alu_1_out_5), .in3(alu_1_out_6), .out(multiplexer_7_out),
    .sel(control_unit_1_alu_mux), .en(_2));
  Register #(.width(32)) RZ (
    .D(multiplexer_7_out), .en(_2), .Q(RZ_q), .clk(multiplexer_2_out), .clr(control_unit_1_register_reset));
  Register #(.width(32)) R1 (.D(r1_in), .en(r1_en), .Q(r1_out), .clk(multiplexer_2_out));  // open: clr
  Register #(.width(32)) R3 (.D(r3_in), .en(r3_en), .Q(r3_out), .clk(multiplexer_2_out));  // open: clr
  Register #(.width(32)) R5 (.D(r5_in), .en(r5_en), .Q(r5_out), .clk(multiplexer_2_out));  // open: clr
  Register #(.width(32)) R7 (.D(r7_in), .en(r7_en), .Q(r7_out), .clk(multiplexer_2_out));  // open: clr
  Multiplexer #(.select(4), .width(32)) multiplexer_8 (
    .in0(r0_out), .in1(r1_out), .in2(r2_out), .in3(r3_out), .in4(r4_out), .in5(r5_out), .in6(r6_out),
    .in7(r7_out), .out(multiplexer_8_out), .sel(multiplexer_5_out), .en(control_unit_1_muxrb_en));  // open: in8, in9, in10, in11, in12, in13, in14, in15
  Register #(.width(32)) RB (
    .D(multiplexer_8_out), .Q(RB_q), .clk(multiplexer_2_out), .clr(control_unit_1_register_reset));  // open: en
  Multiplexer #(.width(32)) multiplexer_9 (
    .in0(RB_q), .in1(bit_extender_1_out), .out(multiplexer_9_out), .sel(control_unit_1_mux_imm_select_line),
    .en(control_unit_1_mux_imm_en));

  // Notes on the sheet:
  //   MEMORY STAGE
  //   FETCH STAGE
  //   Immediate value
  //   fetch_R_en
  //   mem_write
  //   mem_write_mux
  //   OP CODE
  //   muxY_select_line
  //   Data that needs to be stored(STORE)
  //   The address to be read/stored (LOAD/STORE)
  //   Counter keeping track of all clock cycles
  //   which is used to generate control signals
  //   HLT Signal
  //   writeback_dmx
  //   register_reset
  //   Rd
  //   MUX_r1r2_select
  //   MUX_r1r2_en
  //   muxRARB_en
  //   ALU_mux
  //   MUX_Y
  //   20CS02007         
  //   20CS02010
  //   Rd
  //   R1
  //   R2
  //   Write back into register
  //   DECODE STAGE
  //   mux_imm_select_line
  //   mux_imm_en
  //   WRITEBACK STAGE
  //   +
  //   ||
  //   &&
  //   -
  //   EXECUTE STAGE
endmodule

// Control unit
module Control_Unit (
  input  in_1,
  input  in_2,
  input  in_3,
  input  [3:0] in_4,
  output pc_register_en,
  output writeback_dmx_en,
  output mux_r1r2_select,
  output mux_r1r2_en,
  output muxRA_en,
  output muxRB_en,
  output fetch_R_en,
  output mux_imm_select_line,
  output mux_imm_en,
  output mem_write,
  output mem_write_mux,
  output [1:0] ALU_mux,
  output muxY_select_line,
  output muxY_en,
  output register_reset
);

  wire add, add_immediate, \and , and_immediate, load, move, move_immediate, \or , or_1_out, or_immediate,
       store, sub, sub_immediate;

  and and_1 (mem_write, store, in_1);
  and and_2 (mem_write_mux, in_1, or_1_out);
  or or_1 (or_1_out, store, load);
  not not_1 (muxY_select_line, load);
  Decoder #(.select(4)) decoder_1 (
    .out0(move), .out1(move_immediate), .out2(load), .out3(store), .out4(add), .out5(add_immediate),
    .out6(sub), .out7(sub_immediate), .out8(\and ), .out9(and_immediate), .out10(\or ), .out11(or_immediate),
    .out15(muxY_en), .sel(in_4));  // open: out12, out13, out14, en
  or or_2 (mux_imm_select_line, move_immediate, load, store, add_immediate, sub_immediate, and_immediate, or_immediate);
  or or_3 (ALU_mux[0], muxY_en, sub, sub_immediate, \and , and_immediate);
  or or_4 (ALU_mux[1], \and , and_immediate, \or , or_immediate, muxY_en);
  not not_2 (mux_r1r2_select, store);

  assign fetch_R_en = in_2;
  assign mux_imm_en = 1'b1;
  assign mux_r1r2_en = 1'b1;
  assign muxRA_en = 1'b1;
  assign muxRB_en = 1'b1;
  assign pc_register_en = in_3;
  assign register_reset = in_2;
  assign writeback_dmx_en = in_3;

  // Other names for the same wires on the sheet: _0 = in_2; _3 = in_1; _4 = in_3; hlt = muxY_en
endmodule

// Register_en
module register_en (
  input  [3:0] in_1,
  input  in_2,
  input  [3:0] in_3,
  output out_4,
  output out_5,
  output out_6,
  output out_7,
  output out_8,
  output out_9,
  output out_10,
  output out_11
);

  wire add, add_immediate, \and , and_immediate, decoder_1_out0, decoder_1_out1, decoder_1_out2,
       decoder_1_out3, decoder_1_out4, decoder_1_out5, decoder_1_out6, decoder_1_out7, hlt, load, move,
       move_immediate, no_write, \or , or_immediate, store, sub, sub_immediate;

  Decoder #(.select(4)) decoder_1 (
    .out0(decoder_1_out0), .out1(decoder_1_out1), .out2(decoder_1_out2), .out3(decoder_1_out3),
    .out4(decoder_1_out4), .out5(decoder_1_out5), .out6(decoder_1_out6), .out7(decoder_1_out7), .sel(in_1));  // open: out8, out9, out10, out11, out12, out13, out14, out15, en
  not not_1 (no_write, store);
  and and_1 (out_4, decoder_1_out0, no_write, in_2);
  and and_2 (out_6, decoder_1_out2, no_write, in_2);
  and and_3 (out_8, decoder_1_out4, no_write, in_2);
  and and_4 (out_10, decoder_1_out6, no_write, in_2);
  and and_5 (out_5, decoder_1_out1, no_write, in_2);
  and and_6 (out_7, decoder_1_out3, no_write, in_2);
  and and_7 (out_9, decoder_1_out5, no_write, in_2);
  and and_8 (out_11, decoder_1_out7, no_write, in_2);
  Decoder #(.select(4)) decoder_2 (
    .out0(move), .out1(move_immediate), .out2(load), .out3(store), .out4(add), .out5(add_immediate),
    .out6(sub), .out7(sub_immediate), .out8(\and ), .out9(and_immediate), .out10(\or ), .out11(or_immediate),
    .out15(hlt), .sel(in_3));  // open: out12, out13, out14, en
endmodule

module ALU (
  input  [31:0] in_1,
  input  [31:0] in_2,
  output [31:0] out_3,
  output [31:0] out_4,
  output [31:0] out_5,
  output [31:0] out_6
);

  Adder #(.width(32)) adder_1 (.a(in_1), .b(in_2), .out(out_3));  // open: cin, cout
  Subtractor #(.width(32)) subtractor_1 (.a(in_1), .b(in_2), .out(out_4));  // open: bin, bout
  assign out_5 = in_1 | in_2;  // OR_Gate or_1, 32 bits wide
  assign out_6 = in_1 & in_2;  // AND_Gate and_1, 32 bits wide
endmodule
